// Digital circuit 04_Complete.dig as structural Verilog
module _04_Complete (
  input  Clock,
  input  D,
  input  Clear,
  output Q,
  output Q_2
);

  wire nand_1_out, nand_2_out, not_1_out, not_2_out, or_1_out;

  not not_1 (not_1_out, D);
  or or_1 (or_1_out, not_1_out, Clear);
  nand nand_1 (nand_1_out, not_2_out, Clock, D);
  not not_2 (not_2_out, Clear);
  nand nand_2 (nand_2_out, Clock, or_1_out);
  nand nand_3 (Q, nand_1_out, Q_2);
  nand nand_4 (Q_2, Q, nand_2_out);
endmodule
