// Digital circuit 05_Complete.dig as structural Verilog
module _05_Complete (
  input  Clear,
  input  Clock,
  input  T,
  output Q,
  output Q_2
);

  wire and_1_out, and_2_out, and_3_out, and_4_out, and_5_out, and_6_out, nor_1_out, nor_2_out, not_1_out,
       not_2_out;

  and and_1 (and_1_out, Q, T);
  and and_2 (and_2_out, T, Q_2);
  not not_1 (not_1_out, Clock);
  and and_3 (and_3_out, Q, and_1_out, not_1_out);
  and and_4 (and_4_out, not_1_out, and_2_out, Q_2);
  nor nor_1 (nor_1_out, and_3_out, Clear, nor_2_out);
  nor nor_2 (nor_2_out, nor_1_out, and_4_out);
  not not_2 (not_2_out, not_1_out);
  and and_5 (and_5_out, not_2_out, nor_1_out);
  and and_6 (and_6_out, nor_2_out, not_2_out);
  nor nor_3 (Q_2, and_5_out, Q);
  nor nor_4 (Q, Q_2, and_6_out);
endmodule
